# Fritzing sketch R.Ian_breadboard (saved by Fritzing 0.9.2b)
breadboards: 1

parts:
  Composant2 = Arduino Nano (Rev3.0)
  U2 = Voltage Regulator - 5V [package="TO220 [THT]"]
  S4 = Toggle Switch [package=THT]
  VCC2 = Battery
  S5 = Pushbutton [package="[THT]"]
  S6 = Pushbutton [package="[THT]"]
  J1 = Infrared Proximity Sensor

nets:
  GND: Composant2.GND, U2.GND, VCC2.-, S5.Pin_3, S6.Pin_1, J1.GND
  N1: Composant2.D4, S5.Pin_1
  N2: Composant2.D5, S6.Pin_3
  5V: Composant2.5V, U2.output_voltage, J1.Vcc
  N3: Composant2.A0, J1.Vout
  N4: U2.input_voltage, S4.L1
  N5: S4.COM, VCC2.+

notes:
  sensorServo
  leftServo
  rightServo
  rightContactSwith
  leftContactSwith
